# Fritzing sketch ESP32 AD9833 and TFT (saved by Fritzing 0.9.6b)
breadboards: 1

parts:
  U2 = AD9833 Module
  LCD1 = TFT 1.8 inch 160x128 w SD
  Signal_Output = Screw terminal - 2 pins [package=THT]
  RE1 = KY-040 Rotary encoder [package=THT]
  S1_(Step) = Pushbutton [package="[THT]"]
  S2_(Wave) = Pushbutton [package="[THT]"]
  S3_(Sweep) = Pushbutton [package="[THT]"]
  S4_(Frequency_Channel) = Pushbutton [package="[THT]"]
  S5_(Phase_Channel) = Pushbutton [package="[THT]"]
  S6_(Encoder_Value_Select) = Pushbutton [package="[THT]"]
  Phase_Modulation_Input = Screw terminal - 2 pins [package=THT]
  Frequency_Modulation_Input = Screw terminal - 2 pins [package=THT]
  Q1 = PNP-Transistor [package="TO92 [THT]"]
  R1 = Resistor [tolerance=±5% resistance=20k power=0.25 package=THT]
  MCU1 = Wemos Lolin32lite
  R2 = Resistor [tolerance=±5% resistance=56k power=0.25 package=THT]
  R3 = Resistor [tolerance=±5% resistance=56k power=0.25 package=THT]

nets:
  N1: U2.VCC, LCD1.pin_1
  N2: U2.DGND, LCD1.pin2, RE1.GND, S1_(Step).Pin_4, S2_(Wave).Pin_4, S3_(Sweep).Pin_3, S3_(Sweep).Pin_4, S4_(Frequency_Channel).Pin_4, S5_(Phase_Channel).Pin_4, S6_(Encoder_Value_Select).Pin_4, Phase_Modulation_Input.pin2, Frequency_Modulation_Input.pin2, R3.Pin_1
  N3: U2.SDATA, MCU1.pin_25
  N4: U2.SCLK, MCU1.pin_24
  N5: U2.FSYNC, MCU1.pin_23
  N6: U2.AGND, Signal_Output.pin2
  N7: U2.OUT, Signal_Output.pin1
  N8: LCD1.pin3, MCU1.pin_17
  N9: LCD1.pin4, MCU1.pin_18
  N10: LCD1.pin_5, MCU1.pin_19
  N11: LCD1.pin_6, MCU1.pin_16
  N12: LCD1.pin_7, MCU1.pin_11
  N13: LCD1.pin_8, Q1.C
  N14: RE1.Vcc, Q1.E, MCU1.pin_28
  N15: RE1.DT, MCU1.pin_6
  N16: RE1.CLK, MCU1.pin_7
  N17: S1_(Step).Pin_2, MCU1.pin_21
  N18: S2_(Wave).Pin_2, MCU1.pin_12
  N19: S3_(Sweep).Pin_2, MCU1.pin_10
  N20: S4_(Frequency_Channel).Pin_2, MCU1.pin_27
  N21: S5_(Phase_Channel).Pin_2, MCU1.pin_9
  N22: S6_(Encoder_Value_Select).Pin_2, MCU1.pin_8
  N23: Phase_Modulation_Input.pin1, MCU1.pin_20
  N24: Frequency_Modulation_Input.pin1, MCU1.pin_26
  N25: Q1.B, R1.Pin_1
  N26: R1.Pin_0, MCU1.pin_22
  N27: MCU1.pin_5, R2.Pin_1, R3.Pin_0
  N28: MCU1.pin_14, R2.Pin_0

custom parts:
  AD9833 Module: programmable waveform generator
  TFT 1.8 inch 160x128 w SD: This is a generic 1.8 tft spi lcd display available on ebay and others. The 1.8" display has 128x160 color pixels.
  KY-040 Rotary encoder: KY-040 Rotary Encoder with switch on breakout borad from AZ Delivery
  Wemos Lolin32lite: Wemos Lolinlite32 wifi and blue tooth board based on the ESP-32 cpu, digital I/Os 19, analog inputs 6, clock 240mhz, Flash 4Mbytes, lipo battery charger (500ma connection broken out on breadboard but not pcb), usb.
